# Fritzing sketch CET 4711 - Arduino Pong Schematic (saved by Fritzing 0.9.3b)
breadboards: 1

parts:
  Pot_1 = Rotary Potentiometer (Small) [maximum_resistance=10kΩ package=THT]
  S1 = Pushbutton [package="[THT]"]
  Pot_2 = Rotary Potentiometer (Small) [maximum_resistance=10kΩ package=THT]
  Part1 = Arduino Uno (Rev3)
  R1 = Resistor [tolerance=±5% resistance=330 package=THT]

nets (from the schematic view):
  N1: Pot_1.leg1, S1.Pin_1, S1.Pin_2, Pot_2.leg1, Part1.5V, R1.Pin_1
  N2: Pot_1.wiper, Part1.A1
  N3: Pot_1.leg2, Pot_2.leg2, Part1.GND, R1.Pin_0
  N4: S1.Pin_3, S1.Pin_4, Part1.D9_PWM
  N5: Pot_2.wiper, Part1.A2
